// Logisim project computer.circ as structural Verilog
module cpu (
  input  in_1,
  input  RESET
);

  wire clk_1_clock_out, clock_1_out, or_1_out;
  wire [3:0] alu_memory_access_1_data_out, pull_resistor_4_node, pull_resistor_8_node, pull_resistor_12_node,
       pull_resistor_16_node, pull_resistor_20_node, register_memory_access_1_data_out;
  wire [15:0] program_counter_1_always_out;

  Clock clock_1 (.out(clock_1_out));
  clk clk_1 (.CLOCK_IN(clock_1_out), .CLOCK_ENABLE(in_1), .CLOCK_OUT(clk_1_clock_out));  // open: MANUAL_TICK, HALT
  Hex_Digit_Display hex_digit_display_1 (.value(pull_resistor_4_node));  // open: dp
  LED led_1 (.in(pull_resistor_4_node[3]));
  LED led_2 (.in(pull_resistor_4_node[2]));
  LED led_3 (.in(pull_resistor_4_node[1]));
  LED led_4 (.in(pull_resistor_4_node[0]));
  Pull_Resistor pull_resistor_1 (.node(pull_resistor_4_node[3]));
  Pull_Resistor pull_resistor_2 (.node(pull_resistor_4_node[2]));
  Pull_Resistor pull_resistor_3 (.node(pull_resistor_4_node[1]));
  Pull_Resistor pull_resistor_4 (.node(pull_resistor_4_node[0]));
  LED led_5 (.in(pull_resistor_8_node[3]));
  LED led_6 (.in(pull_resistor_8_node[2]));
  Pull_Resistor pull_resistor_5 (.node(pull_resistor_8_node[3]));
  Pull_Resistor pull_resistor_6 (.node(pull_resistor_8_node[2]));
  Hex_Digit_Display hex_digit_display_2 (.value(pull_resistor_8_node));  // open: dp
  LED led_7 (.in(pull_resistor_8_node[1]));
  LED led_8 (.in(pull_resistor_8_node[0]));
  LED led_9 (.in(pull_resistor_12_node[3]));
  Pull_Resistor pull_resistor_7 (.node(pull_resistor_8_node[1]));
  Pull_Resistor pull_resistor_8 (.node(pull_resistor_8_node[0]));
  Pull_Resistor pull_resistor_9 (.node(pull_resistor_12_node[3]));
  Hex_Digit_Display hex_digit_display_3 (.value(pull_resistor_12_node));  // open: dp
  LED led_10 (.in(pull_resistor_12_node[2]));
  LED led_11 (.in(pull_resistor_12_node[1]));
  LED led_12 (.in(pull_resistor_12_node[0]));
  Pull_Resistor pull_resistor_10 (.node(pull_resistor_12_node[2]));
  Pull_Resistor pull_resistor_11 (.node(pull_resistor_12_node[1]));
  Pull_Resistor pull_resistor_12 (.node(pull_resistor_12_node[0]));
  Hex_Digit_Display hex_digit_display_4 (.value(pull_resistor_16_node));  // open: dp
  LED led_13 (.in(pull_resistor_16_node[3]));
  LED led_14 (.in(pull_resistor_16_node[2]));
  LED led_15 (.in(pull_resistor_16_node[1]));
  Pull_Resistor pull_resistor_13 (.node(pull_resistor_16_node[3]));
  Pull_Resistor pull_resistor_14 (.node(pull_resistor_16_node[2]));
  Pull_Resistor pull_resistor_15 (.node(pull_resistor_16_node[1]));
  LED led_16 (.in(pull_resistor_16_node[0]));
  LED led_17 (.in(program_counter_1_always_out[15]));
  Pull_Resistor pull_resistor_16 (.node(pull_resistor_16_node[0]));
  LED led_18 (.in(program_counter_1_always_out[14]));
  LED led_19 (.in(program_counter_1_always_out[13]));
  LED led_20 (.in(program_counter_1_always_out[12]));
  LED led_21 (.in(program_counter_1_always_out[11]));
  LED led_22 (.in(program_counter_1_always_out[10]));
  LED led_23 (.in(program_counter_1_always_out[9]));
  LED led_24 (.in(program_counter_1_always_out[8]));
  LED led_25 (.in(program_counter_1_always_out[7]));
  LED led_26 (.in(program_counter_1_always_out[4]));
  LED led_27 (.in(program_counter_1_always_out[3]));
  LED led_28 (.in(program_counter_1_always_out[6]));
  LED led_29 (.in(program_counter_1_always_out[5]));
  LED led_30 (.in(program_counter_1_always_out[2]));
  LED led_31 (.in(program_counter_1_always_out[1]));
  LED led_32 (.in(program_counter_1_always_out[0]));
  program_counter program_counter_1 (
    .RESET(RESET), .CLOCK(clk_1_clock_out),
    .ADDRESS_IN({pull_resistor_4_node, pull_resistor_8_node, pull_resistor_12_node, pull_resistor_16_node}),
    .ALWAYS_OUT(program_counter_1_always_out),
    .ADDRESS_OUT({pull_resistor_4_node, pull_resistor_8_node, pull_resistor_12_node, pull_resistor_16_node}));  // open: COUNTER_OUT, JUMP, COUNTER_ENABLE
  memory_address_register memory_address_register_1 (
    .DATA_IN(pull_resistor_20_node), .CLOCK(clk_1_clock_out), .RESET(RESET),
    .DATA_OUT({pull_resistor_4_node, pull_resistor_8_node, pull_resistor_12_node, pull_resistor_16_node}));  // open: MAR_WRITE, MAR_OUT
  LED led_33 (.in(pull_resistor_20_node[3]));
  LED led_34 (.in(pull_resistor_20_node[2]));
  LED led_35 (.in(pull_resistor_20_node[1]));
  Pull_Resistor pull_resistor_17 (.node(pull_resistor_20_node[3]));
  Pull_Resistor pull_resistor_18 (.node(pull_resistor_20_node[2]));
  Pull_Resistor pull_resistor_19 (.node(pull_resistor_20_node[1]));
  LED led_36 (.in(pull_resistor_20_node[0]));
  Pull_Resistor pull_resistor_20 (.node(pull_resistor_20_node[0]));
  register_memory_access register_memory_access_1 (
    .DATA_IN(pull_resistor_20_node), .CLOCK(clk_1_clock_out), .RESET(RESET),
    .DATA_OUT(register_memory_access_1_data_out));  // open: WRITE
  alu_memory_access alu_memory_access_1 (
    .DATA_IN(pull_resistor_20_node), .CLOCK(clk_1_clock_out), .RESET(RESET),
    .DATA_OUT(alu_memory_access_1_data_out));  // open: WRITE
  or or_1 (or_1_out, alu_memory_access_1_data_out[3], alu_memory_access_1_data_out[2]);
  Multiplexer #(.width(2)) multiplexer_1 (
    .in0(register_memory_access_1_data_out[3:2]), .in1(alu_memory_access_1_data_out[1:0]), .sel(or_1_out));  // open: out
  alu alu_1 (
    .ENABLE(or_1_out), .SELECT_OP(alu_memory_access_1_data_out[3:2]));  // open: A_IN, B_IN, BORROW_IN, CARRY_IN, BORROW_OUT, DATA_OUT, FLAG_OUT

  // Notes on the sheet:
  //   ADDRESS BUS
  //   DATA BUS
endmodule

module clk (
  input  CLOCK_IN,
  input  CLOCK_ENABLE,
  input  MANUAL_TICK,
  input  HALT,
  output CLOCK_OUT
);

  wire and_1_out, and_2_out, not_1_out, not_2_out, or_1_out;

  not not_1 (not_1_out, CLOCK_ENABLE);
  and and_1 (and_1_out, CLOCK_IN, CLOCK_ENABLE);
  and and_2 (and_2_out, not_1_out, MANUAL_TICK);
  or or_1 (or_1_out, and_1_out, and_2_out);
  not not_2 (not_2_out, HALT);
  and and_3 (CLOCK_OUT, or_1_out, not_2_out);
endmodule

module program_counter (
  input  RESET,
  input  JUMP,
  input  COUNTER_ENABLE,
  input  CLOCK,
  input  [15:0] ADDRESS_IN,
  input  COUNTER_OUT,
  output [15:0] ALWAYS_OUT,
  output [15:0] ADDRESS_OUT
);

  wire not_1_out;

  not not_1 (not_1_out, COUNTER_OUT);
  Counter #(.max('hffff), .width(16)) counter_1 (
    .clr(RESET), .load(JUMP), .up(COUNTER_ENABLE), .count(COUNTER_ENABLE), .clk(CLOCK), .D(ADDRESS_IN),
    .Q(ALWAYS_OUT));  // open: carry
  assign ADDRESS_OUT = not_1_out ? ALWAYS_OUT : 16'bz;  // Controlled_Buffer controlled_buffer_1
endmodule

module memory_address_register (
  input  [3:0] DATA_IN,
  input  [3:0] MAR_WRITE,
  input  CLOCK,
  input  RESET,
  input  MAR_OUT,
  output [15:0] DATA_OUT
);

  wire [3:0] register_1_q, register_2_q, register_3_q, register_4_q;

  Register #(.width(4)) register_1 (.D(DATA_IN), .en(MAR_WRITE[0]), .clk(CLOCK), .Q(register_1_q), .clr(RESET));
  Register #(.width(4)) register_2 (.D(DATA_IN), .en(MAR_WRITE[1]), .clk(CLOCK), .Q(register_2_q), .clr(RESET));
  Register #(.width(4)) register_3 (.D(DATA_IN), .en(MAR_WRITE[2]), .clk(CLOCK), .Q(register_3_q), .clr(RESET));
  Register #(.width(4)) register_4 (.D(DATA_IN), .en(MAR_WRITE[3]), .clk(CLOCK), .Q(register_4_q), .clr(RESET));
  assign DATA_OUT[3:0] = MAR_OUT ? register_1_q : 4'bz;  // Controlled_Buffer controlled_buffer_1
  assign DATA_OUT[7:4] = MAR_OUT ? register_2_q : 4'bz;  // Controlled_Buffer controlled_buffer_2
  assign DATA_OUT[11:8] = MAR_OUT ? register_3_q : 4'bz;  // Controlled_Buffer controlled_buffer_3
  assign DATA_OUT[15:12] = MAR_OUT ? register_4_q : 4'bz;  // Controlled_Buffer controlled_buffer_4
endmodule

module alu (
  input  BORROW_IN,
  input  CARRY_IN,
  input  [3:0] A_IN,
  input  [3:0] B_IN,
  input  ENABLE,
  input  [1:0] SELECT_OP,
  output [3:0] DATA_OUT,
  output BORROW_OUT,
  output [3:0] FLAG_OUT
);

  wire [3:0] adder_1_out, subtractor_1_out;

  Adder #(.width(4)) adder_1 (.a(A_IN), .b(B_IN), .out(adder_1_out), .cin(CARRY_IN), .cout(FLAG_OUT[0]));
  Subtractor #(.width(4)) subtractor_1 (.a(A_IN), .b(B_IN), .out(subtractor_1_out), .bin(BORROW_IN), .bout(BORROW_OUT));
  Comparator #(.width(4)) comparator_1 (.a(A_IN), .b(B_IN), .gt(FLAG_OUT[1]), .eq(FLAG_OUT[2]), .lt(FLAG_OUT[3]));
  Multiplexer #(.enable("true"), .select(2), .width(4)) multiplexer_1 (
    .in1(adder_1_out), .in2(subtractor_1_out), .in3(FLAG_OUT), .out(DATA_OUT), .sel(SELECT_OP), .en(ENABLE));  // open: in0
endmodule

module register_file (
  input  [3:0] DATA_IN,
  input  [1:0] SLCT,
  input  WRITE,
  input  READ,
  input  CLOCK,
  input  RESET,
  output [3:0] DATA_OUT
);

  wire decoder_1_out0, decoder_1_out1, decoder_1_out2, decoder_1_out3, decoder_2_out0, decoder_2_out1,
       decoder_2_out2, decoder_2_out3;
  wire [3:0] demultiplexer_1_out0, demultiplexer_1_out1, demultiplexer_1_out2, demultiplexer_1_out3,
       register_1_q, register_2_q, register_3_q, register_4_q;

  Demultiplexer #(.select(2), .width(4)) demultiplexer_1 (
    .out0(demultiplexer_1_out0), .out1(demultiplexer_1_out1), .out2(demultiplexer_1_out2),
    .out3(demultiplexer_1_out3), .in(DATA_IN), .sel(SLCT));
  Decoder #(.select(2)) decoder_1 (
    .out0(decoder_1_out0), .out1(decoder_1_out1), .out2(decoder_1_out2), .out3(decoder_1_out3), .sel(SLCT),
    .en(WRITE));
  Register #(.width(4)) register_1 (
    .D(demultiplexer_1_out0), .en(decoder_1_out0), .clk(CLOCK), .Q(register_1_q), .clr(RESET));
  Register #(.width(4)) register_2 (
    .D(demultiplexer_1_out1), .en(decoder_1_out1), .clk(CLOCK), .Q(register_2_q), .clr(RESET));
  Register #(.width(4)) register_3 (
    .D(demultiplexer_1_out2), .en(decoder_1_out2), .clk(CLOCK), .Q(register_3_q), .clr(RESET));
  Register #(.width(4)) register_4 (
    .D(demultiplexer_1_out3), .en(decoder_1_out3), .clk(CLOCK), .Q(register_4_q), .clr(RESET));
  Decoder #(.select(2)) decoder_2 (
    .out0(decoder_2_out0), .out1(decoder_2_out1), .out2(decoder_2_out2), .out3(decoder_2_out3), .sel(SLCT),
    .en(READ));
  assign DATA_OUT = decoder_2_out0 ? register_1_q : 4'bz;  // Controlled_Buffer controlled_buffer_1
  assign DATA_OUT = decoder_2_out1 ? register_2_q : 4'bz;  // Controlled_Buffer controlled_buffer_2
  assign DATA_OUT = decoder_2_out2 ? register_3_q : 4'bz;  // Controlled_Buffer controlled_buffer_3
  assign DATA_OUT = decoder_2_out3 ? register_4_q : 4'bz;  // Controlled_Buffer controlled_buffer_4
endmodule

module register_memory_access (
  input  [3:0] DATA_IN,
  input  WRITE,
  input  CLOCK,
  input  RESET,
  output [3:0] DATA_OUT
);

  Register #(.width(4)) register_1 (.D(DATA_IN), .en(WRITE), .clk(CLOCK), .Q(DATA_OUT), .clr(RESET));
endmodule

module alu_memory_access (
  input  [3:0] DATA_IN,
  input  WRITE,
  input  CLOCK,
  input  RESET,
  output [3:0] DATA_OUT
);

  Register #(.width(4)) register_1 (.D(DATA_IN), .en(WRITE), .clk(CLOCK), .Q(DATA_OUT), .clr(RESET));
endmodule
